# Fritzing sketch TripWire (saved by Fritzing 0.9.1b)
breadboards: 1

parts:
  Part1 = Arduino Pro Mini v13
  Q1 = NPN-Transistor [part_number=BC548 package="TO92 [THT]"]
  Q2 = NPN-Transistor [part_number=BC548 package="TO92 [THT]"]
  R1 = Resistor [tolerance=±5% resistance=1M package=THT]
  R2 = Resistor [tolerance=±5% resistance=1M package=THT]
  V1 = DC Power [voltage=5]
  Nokia_5110_LCD_Module1 = Nokia5110
  LED1 = LED - 5mm [color="Red (633nm)" package="5 mm [THT]"]

nets:
  VCC: Part1.VCC, R1.Pin_0, Nokia_5110_LCD_Module1.VCC, LED1.cathode
  GND: Part1.GND, Q2.E, R2.Pin_1, V1.V-, Nokia_5110_LCD_Module1.GND
  N1: Part1.RAW, V1.V+
  N2: Part1.A2, Nokia_5110_LCD_Module1.BL
  N3: Part1.A1, Nokia_5110_LCD_Module1.CE
  N4: Part1.A0, Nokia_5110_LCD_Module1.DC
  N5: Part1.D13/SCK, Nokia_5110_LCD_Module1.CLK
  N6: Part1.D11_PWM/MOSI, Nokia_5110_LCD_Module1.DIN
  N7: Part1.D10_PWM/SS, Nokia_5110_LCD_Module1.RST
  N8: Part1.D2, Q1.C, Q2.C, R1.Pin_1
  N9: Q1.E, Q2.B
  N10: Q1.B, R2.Pin_0, LED1.anode

custom parts:
  : Nokia 5110 LCD with 8 pin. It's a 45mm*45mm module part. Description: The Nokia 5110 is a basic graphic LCD screen for lots of applications. It was originally intended for as a cell phone screen. This one is mounted on an easy to solder PCB. It uses the PCD8544 controller. The PCD8544 is a low power CMOS LCD controller/driver, designed to drive a graphic display of 48 rows and 84 columns. All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
